# Fritzing sketch snake (saved by Fritzing 0.9.3b)
breadboards: 1

parts:
  Part1 = Arduino Uno (Rev3) - ICSP
  S1 = Pushbutton [package="[THT]"]
  S3 = Pushbutton [package="[THT]"]
  S4 = Pushbutton [package="[THT]"]
  Part2 = Bicolor 8x8 LED Matrix Backpack [part_number=902]
  S5 = Pushbutton [package="[THT]"]

nets:
  N1: Part1.A4/SDA, Part2.SDA
  N2: Part1.A5/SCL, Part2.SCL
  GND: Part1.GND, S1.Pin_1, S1.Pin_2, S3.Pin_3, S3.Pin_4, S4.Pin_1, S4.Pin_2, Part2.GND, S5.Pin_1, S5.Pin_2
  N3: Part1.D2, S3.Pin_1, S3.Pin_2
  N4: Part1.D3_PWM, S1.Pin_3, S1.Pin_4
  N5: Part1.D4, S4.Pin_3, S4.Pin_4
  N6: Part1.D5_PWM, S5.Pin_3, S5.Pin_4
  5V: Part1.5V, Part2.VDD

custom parts:
  Bicolor 8x8 LED Matrix Backpack: This 1.2" bi-color 8x8 LED matrix includes a driver chip for simple control via an I2C interface. It's called a Bicolor LED, but you can have 3 colors total by turning on the red and green LEDs, which creates yellow. That's 3 colors for the price of 2! The backpacks come with address-selection jumpers so you can connect up to eight bicolor matrices on a single I2C bus.
